// Digital circuit diglab_02_02.dig as structural Verilog
module diglab_02_02 (
  input  A,
  input  B,
  output Output
);

  wire not_1_out, not_2_out, or_1_out, or_2_out;

  not not_1 (not_1_out, A);
  not not_2 (not_2_out, B);
  or or_1 (or_1_out, A, B);
  or or_2 (or_2_out, not_1_out, not_2_out);
  and and_1 (Output, or_1_out, or_2_out);
endmodule
