// Digital circuit FullAdder_NAND_SoP.dig as structural Verilog
module FullAdder_NAND_SoP (
  input  A,
  input  B,
  input  Cin,
  output Sum,
  output Cout,
  output Cout2,
  output Sum2
);

  wire _7400_1_pin1, _7400_1_pin2, _7400_2_pin3, _7400_2_pin5, _7400_2_pin9, _7400_3_pin6, _7400_3_pin10, nA,
       nand_4_out, nand_5_out, nand_6_out, nand_7_out, nand_8_out, nand_9_out, nand_10_out, nB, nC;

  nand nand_1 (nA, A, A);
  nand nand_2 (nB, B, B);
  nand nand_3 (nC, Cin, Cin);
  nand nand_4 (nand_4_out, nA, nB, Cin);
  nand nand_5 (nand_5_out, nA, B, nC);
  nand nand_6 (nand_6_out, A, nB, nC);
  nand nand_7 (nand_7_out, A, B, Cin);
  nand nand_8 (nand_8_out, A, Cin);
  nand nand_9 (nand_9_out, A, B);
  nand nand_10 (nand_10_out, B, Cin);
  nand nand_11 (Sum, nand_4_out, nand_5_out, nand_6_out, nand_7_out);
  nand nand_12 (Cout, nand_8_out, nand_9_out, nand_10_out);
  _7400 _7400_1 (
    .pin1(_7400_1_pin1), .pin2(_7400_1_pin2), .pin3(Cout2), .pin4(1'b0), .pin5(1'b0), .pin7(1'b0),
    .pin9(1'b0), .pin10(1'b0), .pin12(1'b0), .pin13(1'b0), .pin14(1'b1));  // open: pin6, pin8, pin11
  _7400 _7400_2 (
    .pin1(_7400_1_pin2), .pin2(Cin), .pin3(_7400_2_pin3), .pin4(_7400_2_pin3), .pin5(_7400_2_pin5),
    .pin6(Sum2), .pin7(1'b0), .pin8(_7400_2_pin5), .pin9(_7400_2_pin9), .pin10(_7400_1_pin2),
    .pin11(_7400_1_pin2), .pin12(Cin), .pin13(_7400_2_pin9), .pin14(1'b1));
  _7400 _7400_3 (
    .pin1(B), .pin2(A), .pin3(_7400_1_pin1), .pin4(_7400_1_pin1), .pin5(A), .pin6(_7400_3_pin6), .pin7(1'b0),
    .pin8(_7400_2_pin9), .pin9(_7400_3_pin6), .pin10(_7400_3_pin10), .pin11(_7400_3_pin10),
    .pin12(_7400_1_pin1), .pin13(B), .pin14(1'b1));
endmodule
