// Digital circuit diglab_02_04.dig as structural Verilog
module diglab_02_04 (
  input  A,
  input  B,
  input  Cin,
  output Sum,
  output Cout
);

  wire not_1_out, not_2_out, not_3_out, not_4_out, not_5_out, not_6_out, not_7_out, not_8_out, not_9_out,
       or_1_out, or_2_out, or_3_out, or_4_out, or_5_out, or_6_out, or_7_out, or_8_out;

  not not_1 (not_1_out, A);
  not not_2 (not_2_out, A);
  not not_3 (not_3_out, A);
  not not_4 (not_4_out, B);
  not not_5 (not_5_out, Cin);
  not not_6 (not_6_out, Cin);
  not not_7 (not_7_out, B);
  not not_8 (not_8_out, Cin);
  not not_9 (not_9_out, B);
  or or_1 (or_1_out, A, B, Cin);
  or or_2 (or_2_out, A, not_4_out, not_5_out);
  or or_3 (or_3_out, not_1_out, B, not_6_out);
  or or_4 (or_4_out, not_2_out, not_7_out, Cin);
  or or_5 (or_5_out, A, B, Cin);
  or or_6 (or_6_out, A, B, not_8_out);
  or or_7 (or_7_out, not_3_out, B, Cin);
  or or_8 (or_8_out, A, not_9_out, Cin);
  and and_1 (Sum, or_1_out, or_2_out, or_3_out, or_4_out);
  and and_2 (Cout, or_5_out, or_6_out, or_7_out, or_8_out);
endmodule
