// Digital circuit diglab_02_05.dig as structural Verilog
module diglab_02_05 (
  input  A,
  input  B,
  input  C,
  input  D,
  output Z2,
  output Z1,
  output Z3
);

  wire and_1_out, and_2_out, and_3_out, and_4_out, and_5_out, and_6_out, and_7_out, and_8_out, and_9_out,
       and_10_out;

  and and_1 (and_1_out, ~A, C);  // And
  and and_2 (and_2_out, ~B, C, D);  // And
  and and_3 (and_3_out, ~A, ~B, D);  // And
  and and_4 (and_4_out, A, ~C);  // And
  and and_5 (and_5_out, B, ~C, ~D);  // And
  and and_6 (and_6_out, A, B, ~D);  // And
  and and_7 (and_7_out, ~A, ~B, ~C, ~D);  // And
  and and_8 (and_8_out, ~A, B, ~C, D);  // And
  and and_9 (and_9_out, A, B, C, D);
  and and_10 (and_10_out, A, ~B, C, ~D);  // And
  or or_1 (Z2, and_1_out, and_2_out, and_3_out);
  or or_2 (Z1, and_4_out, and_5_out, and_6_out);
  or or_3 (Z3, and_7_out, and_8_out, and_9_out, and_10_out);
endmodule
