// Digital circuit diglab_02_06.dig as structural Verilog
module diglab_02_06 (
  input  A,
  input  B,
  input  C,
  input  D,
  output Z2,
  output Z1,
  output Z3
);

  wire or_1_out, or_2_out, or_3_out, or_4_out, or_5_out, or_6_out, or_7_out, or_8_out, or_9_out, or_10_out;

  or or_1 (or_1_out, A, ~C);  // Or
  or or_2 (or_2_out, B, ~C, ~D);  // Or
  or or_3 (or_3_out, A, B, ~D);  // Or
  or or_4 (or_4_out, ~A, C);  // Or
  or or_5 (or_5_out, ~B, C, D);  // Or
  or or_6 (or_6_out, ~A, ~B, D);  // Or
  or or_7 (or_7_out, A, B, C, D);
  or or_8 (or_8_out, A, ~B, C, ~D);  // Or
  or or_9 (or_9_out, ~A, ~B, ~C, ~D);  // Or
  or or_10 (or_10_out, ~A, B, ~C, D);  // Or
  nand nand_1 (Z2, or_1_out, or_2_out, or_3_out);
  nand nand_2 (Z1, or_4_out, or_5_out, or_6_out);
  nand nand_3 (Z3, or_7_out, or_8_out, or_9_out, or_10_out);
endmodule
