// Digital circuit diglab_02_07.dig as structural Verilog
module diglab_02_07 (
  input  X0,
  input  X1,
  input  Selector,
  output Z
);

  wire and_1_out, and_2_out;

  and and_1 (and_1_out, X0, ~Selector);  // And
  and and_2 (and_2_out, X1, Selector);
  or or_1 (Z, and_1_out, and_2_out);
endmodule
