// Digital circuit diglab_02_08.dig as structural Verilog
module diglab_02_08 (
  input  X0,
  input  X1,
  input  Selector,
  output Z
);

  wire or_1_out, or_2_out;

  or or_1 (or_1_out, ~X0, Selector);  // Or
  or or_2 (or_2_out, ~X1, ~Selector);  // Or
  nand nand_1 (Z, or_1_out, or_2_out);
endmodule
