// Digital circuit diglab_02_09.dig as structural Verilog
module diglab_02_09 (
  input  X0,
  input  X1,
  input  X2,
  input  X3,
  input  S1,
  input  S0,
  output Z
);

  wire and_1_out, and_2_out, and_3_out, and_4_out;

  and and_1 (and_1_out, ~S1, ~S0, X0);  // And
  and and_2 (and_2_out, ~S1, S0, X1);  // And
  and and_3 (and_3_out, S1, ~S0, X2);  // And
  and and_4 (and_4_out, S1, S0, X3);
  or or_1 (Z, and_1_out, and_2_out, and_3_out, and_4_out);
endmodule
