// Digital circuit diglab_03_01.dig as structural Verilog
module diglab_03_01 (
  input  [3:0] In,
  output A,
  output B,
  output D,
  output E,
  output F,
  output G,
  output C
);

  wire and_1_out, and_2_out, and_3_out, and_4_out, and_5_out, and_6_out, and_7_out, and_8_out, and_9_out,
       and_10_out, and_11_out, and_12_out, and_13_out, and_14_out, and_15_out, and_16_out, and_17_out;

  Seven_Seg seven_seg_1 (.a(A), .b(B), .c(C), .d(D), .e(E), .f(F), .g(G), .dp(1'b0));
  and and_1 (and_1_out, ~In[3], ~In[2], ~In[1], In[0]);  // And
  and and_2 (and_2_out, ~In[3], In[2], ~In[1], ~In[0]);  // And
  and and_3 (and_3_out, ~In[3], In[2], ~In[1], In[0]);  // And
  and and_4 (and_4_out, ~In[3], In[2], In[1], ~In[0]);  // And
  nand nand_1 (C, ~In[3], ~In[2], In[1], ~In[0]);  // NAnd
  and and_5 (and_5_out, ~In[3], ~In[2], ~In[1], In[0]);  // And
  and and_6 (and_6_out, ~In[3], In[2], ~In[1], ~In[0]);  // And
  and and_7 (and_7_out, ~In[3], In[2], In[1], In[0]);  // And
  and and_8 (and_8_out, ~In[3], ~In[2], ~In[1], ~In[0]);  // And
  and and_9 (and_9_out, ~In[3], ~In[2], In[1], ~In[0]);  // And
  and and_10 (and_10_out, ~In[3], In[2], In[1], ~In[0]);  // And
  and and_11 (and_11_out, In[3], ~In[2], ~In[1], ~In[0]);  // And
  and and_12 (and_12_out, ~In[3], ~In[2], ~In[1], In[0]);  // And
  and and_13 (and_13_out, ~In[3], ~In[2], In[1], ~In[0]);  // And
  and and_14 (and_14_out, ~In[3], ~In[2], In[1], In[0]);  // And
  and and_15 (and_15_out, ~In[3], ~In[2], ~In[1], ~In[0]);  // And
  and and_16 (and_16_out, ~In[3], ~In[2], ~In[1], In[0]);  // And
  and and_17 (and_17_out, ~In[3], In[2], In[1], In[0]);  // And
  nor nor_1 (A, and_1_out, and_2_out);
  nor nor_2 (B, and_3_out, and_4_out);
  nor nor_3 (D, and_5_out, and_6_out, and_7_out);
  or or_1 (E, and_8_out, and_9_out, and_10_out, and_11_out);
  nor nor_4 (F, and_12_out, and_13_out, and_14_out);
  nor nor_5 (G, and_15_out, and_16_out, and_17_out);
endmodule
