// Digital circuit diglab_04_01.dig as structural Verilog
module diglab_04_01 (
  input  [3:0] In,
  input  [1:0] Selector,
  output [3:0] Output
);

  wire and_1_out, and_2_out, and_3_out, and_4_out, and_5_out, and_6_out, and_7_out, and_8_out, and_9_out,
       and_10_out, and_11_out, and_12_out, and_13_out, and_14_out, and_15_out, and_16_out, and_17_out,
       and_18_out, and_19_out, and_20_out, and_21_out, and_22_out, and_23_out, and_24_out, and_25_out,
       and_26_out, and_27_out, and_28_out, and_29_out, and_30_out, and_31_out;

  and and_1 (and_1_out, ~In[3], In[1], In[0], Selector[1], Selector[0]);  // And
  and and_2 (and_2_out, ~In[3], In[2], ~In[1], In[0], Selector[1]);  // And
  and and_3 (and_3_out, ~In[3], In[2], In[1], ~Selector[0]);  // And
  and and_4 (and_4_out, ~In[3], In[2], In[0], ~Selector[0]);  // And
  and and_5 (and_5_out, In[3], ~In[2], ~In[1]);  // And
  and and_6 (and_6_out, In[3], ~In[2], ~In[1], ~Selector[1], Selector[0]);  // And
  and and_7 (and_7_out, In[3], ~In[2], ~In[1], Selector[1], ~Selector[0]);  // And
  and and_8 (and_8_out, ~In[2], ~In[1], In[0], ~Selector[1], ~Selector[0]);  // And
  and and_9 (and_9_out, ~In[2], ~In[1], In[0], Selector[1], Selector[0]);  // And
  and and_10 (and_10_out, ~In[3], ~In[2], In[1], ~Selector[1], ~Selector[0]);  // And
  and and_11 (and_11_out, ~In[3], In[2], In[1], Selector[1]);  // And
  and and_12 (and_12_out, ~In[3], In[2], ~In[1], In[0], ~Selector[1], Selector[0]);  // And
  and and_13 (and_13_out, ~In[3], In[2], ~In[1], ~In[0], ~Selector[1]);  // And
  and and_14 (and_14_out, ~In[3], In[2], ~In[0], Selector[1]);  // And
  and and_15 (and_15_out, ~In[3], In[2], In[1], Selector[0]);  // And
  and and_16 (and_16_out, ~In[3], In[1], ~In[0], Selector[1], Selector[0]);  // And
  and and_17 (and_17_out, ~In[3], In[1], In[0], ~Selector[1], ~Selector[0]);  // And
  and and_18 (and_18_out, ~In[3], ~In[2], In[1], ~Selector[1], Selector[0]);  // And
  and and_19 (and_19_out, ~In[2], ~In[1], ~In[0], ~Selector[1], ~Selector[0]);  // And
  and and_20 (and_20_out, ~In[3], ~In[2], In[1], Selector[1], ~Selector[0]);  // And
  and and_21 (and_21_out, ~In[3], In[2], ~In[1], In[0], ~Selector[1], Selector[0]);  // And
  and and_22 (and_22_out, ~In[3], In[2], ~In[1], ~In[0], ~Selector[1]);  // And
  and and_23 (and_23_out, ~In[3], In[2], ~In[1], In[0], Selector[1]);  // And
  and and_24 (and_24_out, In[3], ~In[2], ~In[1], Selector[1]);  // And
  and and_25 (and_25_out, ~In[3], ~In[0], ~Selector[1], ~Selector[0]);  // And
  and and_26 (and_26_out, ~In[2], ~In[1], In[0], Selector[1]);  // And
  and and_27 (and_27_out, ~In[2], ~In[1], ~In[0], ~Selector[1], ~Selector[0]);  // And
  and and_28 (and_28_out, ~In[3], In[2], ~In[1], In[0], ~Selector[1], Selector[0]);  // And
  and and_29 (and_29_out, ~In[3], In[1], ~In[0], ~Selector[1]);  // And
  and and_30 (and_30_out, ~In[2], ~In[1], In[0], Selector[0]);  // And
  and and_31 (and_31_out, ~In[3], In[0], Selector[1]);  // And
  or or_1 (Output[3], and_1_out, and_2_out, and_3_out, and_4_out, and_5_out);
  or or_2 (Output[2], and_6_out, and_7_out, and_8_out, and_9_out, and_10_out, and_11_out, and_12_out, and_13_out, and_14_out, and_15_out);
  or or_3 (Output[1], and_16_out, and_17_out, and_18_out, and_19_out, and_20_out, and_21_out, and_22_out, and_23_out, and_24_out);
  or or_4 (Output[0], and_25_out, and_26_out, and_27_out, and_28_out, and_29_out, and_30_out, and_31_out);

  // Other names for the same wires on the sheet: d1 = Output[0]; d2 = Output[1]; d3 = Output[2]; d4 = Output[3]
endmodule
