// Digital circuit diglab_04_02.dig as structural Verilog
module diglab_04_02 (
  input  [6:0] In,
  output [6:0] Output
);

  wire C1, C2, C3;
  wire [6:0] multiplexer_1_out;

  Multiplexer #(.Bits(7), .Selector_Bits(3)) multiplexer_1 (
    .sel({C1, C2, C3}), .in_0({7{1'b0}}), .in_1(7'b1000000), .in_2(7'b0100000), .in_3(7'b0010000),
    .in_4(7'b0001000), .in_5(7'b0000100), .in_6(7'b0000010), .in_7(7'b0000001), .out(multiplexer_1_out));
  xor xor_1 (C1, In[3], In[2], In[1], In[0]);
  xor xor_2 (C2, In[5], In[4], In[1], In[0]);
  xor xor_3 (C3, In[6], In[4], In[2], In[0]);
  assign Output = In ^ multiplexer_1_out;  // XOr xor_4, 7 bits wide
endmodule
