// Digital circuit diglab_06_03.dig as structural Verilog
module diglab_06_03 (
  input  K,
  input  Clock,
  input  Clear,
  input  J,
  output Q,
  output Q_2
);

  wire and_1_out, and_2_out, and_3_out, and_4_out, nor_1_out, nor_2_out, not_1_out, or_1_out, or_2_out;

  and and_1 (and_1_out, Q, K, Clock);
  and and_2 (and_2_out, Clock, J, Q_2);
  or or_1 (or_1_out, Clear, and_1_out);
  not not_1 (not_1_out, Clock);
  nor nor_1 (nor_1_out, or_1_out, nor_2_out);
  nor nor_2 (nor_2_out, nor_1_out, and_2_out);
  // Probe P on nor_1_out
  // Probe \P on nor_2_out
  and and_3 (and_3_out, nor_1_out, not_1_out);
  and and_4 (and_4_out, nor_2_out, not_1_out);
  or or_2 (or_2_out, Clear, and_4_out);
  nor nor_3 (Q, or_2_out, Q_2);
  nor nor_4 (Q_2, Q, and_3_out);
endmodule
