// Digital circuit diglab_06_04.dig as structural Verilog
module diglab_06_04 (
  input  D,
  input  Clock,
  input  Clear,
  output Q,
  output Q_2
);

  wire and_1_out, nor_1_out, nor_2_out, nor_3_out, nor_4_out, not_1_out;

  and and_1 (and_1_out, D, ~Clear);  // And
  not not_1 (not_1_out, Clock);
  nor nor_1 (nor_1_out, nor_4_out, nor_2_out);
  nor nor_2 (nor_2_out, nor_1_out, not_1_out);
  nor nor_3 (nor_3_out, nor_2_out, not_1_out, nor_4_out);
  nor nor_4 (nor_4_out, nor_3_out, and_1_out);
  nor nor_5 (Q, nor_2_out, Q_2);
  nor nor_6 (Q_2, Q, nor_3_out);

  // Notes on the sheet:
  //   D Flip-flop
endmodule
