// Digital circuit diglab_07_01.dig as structural Verilog
module diglab_07_01 (
  input  clk,
  input  reset,
  output C,
  output B,
  output A
);

  wire and_1_out, and_2_out, and_3_out, change0, change1, change2, reset_t, xor_1_out, xor_2_out, xor_3_out;

  not not_1 (reset_t, reset);
  and and_1 (and_1_out, reset_t, xor_1_out);
  xor xor_1 (xor_1_out, change0, A);
  D_FF d_ff_1 (.D(and_1_out), .C(clk), .Q(A));  // open: nQ
  and and_2 (and_2_out, reset_t, xor_2_out);
  xor xor_2 (xor_2_out, change1, B);
  D_FF d_ff_2 (.D(and_2_out), .C(clk), .Q(B));  // open: nQ
  and and_3 (and_3_out, reset_t, xor_3_out);
  xor xor_3 (xor_3_out, change2, C);
  Multiplexer #(.Bits(3), .Selector_Bits(3)) multiplexer_1 (
    .sel({C, B, A}), .in_0(3'b010), .in_1(3'b000), .in_2(3'b001), .in_3(3'b110), .in_4(3'b000),
    .in_5(3'b011), .in_6(3'b110), .in_7(3'b000), .out({change2, change1, change0}));
  D_FF d_ff_3 (.D(and_3_out), .C(clk), .Q(C));  // open: nQ
endmodule
