// Digital circuit diglab_07_01_v2.dig as structural Verilog
module diglab_07_01_v2 (
  input  clk,
  input  reset,
  output C,
  output B,
  output A
);

  wire A_new, B_new, C_new;
  wire [2:0] multiplexer_1_out;

  D_FF bitC (.D(C_new), .C(clk), .Q(C));  // open: nQ
  D_FF bitB (.D(B_new), .C(clk), .Q(B));  // open: nQ
  D_FF bitA (.D(A_new), .C(clk), .Q(A));  // open: nQ
  Multiplexer #(.Bits(3), .Selector_Bits(3)) multiplexer_1 (
    .sel({C, B, A}), .in_0(3'b010), .in_1(3'b000), .in_2(3'b011), .in_3(3'b101), .in_4(3'b000),
    .in_5(3'b110), .in_6(3'b000), .in_7(3'b000), .out(multiplexer_1_out));
  // Probe on multiplexer_1_out
  Multiplexer #(.Bits(3)) multiplexer_2 (
    .sel(reset), .in_0(multiplexer_1_out), .in_1(3'b000), .out({C_new, B_new, A_new}));
endmodule
