// Digital circuit diglab_07_02.dig as structural Verilog
module diglab_07_02 (
  input  clock,
  input  reset,
  input  X,
  input  load,
  input  Y,
  input  Z,
  output C,
  output B,
  output A
);

  wire A_t, and_1_out, and_2_out, and_3_out, and_4_out, and_5_out, and_6_out, and_7_out, and_8_out,
       and_9_out, B_t, C_t, not_2_out, not_3_out, not_4_out, or_1_out, or_2_out, or_3_out, reset_t;

  and and_1 (and_1_out, Z, load);
  not not_1 (reset_t, reset);
  and and_2 (and_2_out, reset_t, or_1_out);
  or or_1 (or_1_out, and_1_out, and_3_out);
  D_FF d_ff_1 (.D(and_2_out), .C(clock), .Q(C));  // open: nQ
  and and_3 (and_3_out, not_2_out, C_t);
  not not_2 (not_2_out, load);
  and and_4 (and_4_out, Y, load);
  and and_5 (and_5_out, reset_t, or_2_out);
  or or_2 (or_2_out, and_4_out, and_6_out);
  D_FF d_ff_2 (.D(and_5_out), .C(clock), .Q(B));  // open: nQ
  and and_6 (and_6_out, not_3_out, B_t);
  not not_3 (not_3_out, load);
  and and_7 (and_7_out, reset_t, or_3_out);
  or or_3 (or_3_out, and_8_out, and_9_out);
  and and_8 (and_8_out, X, load);
  Multiplexer #(.Bits(3), .Selector_Bits(3)) multiplexer_1 (
    .sel({A, B, C}), .in_0(3'b010), .in_1(3'b100), .in_2(3'b011), .in_3(3'b101), .in_4(3'b010),
    .in_5(3'b111), .in_6(3'b111), .in_7(3'b001), .out({A_t, B_t, C_t}));
  D_FF d_ff_3 (.D(and_7_out), .C(clock), .Q(A));  // open: nQ
  and and_9 (and_9_out, not_4_out, A_t);
  not not_4 (not_4_out, load);
endmodule
