// Digital circuit diglab_08_01.dig as structural Verilog
module diglab_08_01 (
  input  clk,
  input  [7:0] A,
  input  [7:0] B,
  input  clear,
  input  start,
  output busy,
  output [7:0] \output 
);

  wire a_eq__eq_b, a_gt_b, and_1_out, and_2_out, and_3_out, clear_t, loadA, loadB, multiplexer_3_out,
       multiplexer_4_out, not_2_out, not_3_out, not_4_out, Qa, Qb, S00, S01, S10, S11;
  wire [7:0] a_t, b_t, newA, newB, sub_1_s, sub_2_s;

  not not_1 (clear_t, clear);
  Register #(.Bits(8)) reg_a (.D(newA), .C(clk), .en(loadA), .Q(a_t));
  Register #(.Bits(8)) reg_b (.D(newB), .C(clk), .en(loadB), .Q(b_t));
  Register #(.Bits(8)) reg_out (.D(a_t), .C(clk), .en(busy), .Q(\output ));
  // Probe on a_t
  // Probe on b_t
  Comparator #(.Bits(8)) comparator_1 (.a(a_t), .b(b_t), .gt(a_gt_b), .eq(a_eq__eq_b));  // open: lt
  Sub #(.Bits(8)) sub_1 (.a(a_t), .b(b_t), .c_i(1'b0), .s(sub_1_s));  // open: c_o
  Sub #(.Bits(8)) sub_2 (.a(b_t), .b(a_t), .c_i(1'b0), .s(sub_2_s));  // open: c_o
  Multiplexer #(.Bits(8)) multiplexer_1 (.sel(busy), .in_0(A), .in_1(sub_1_s), .out(newA));
  Multiplexer #(.Bits(8)) multiplexer_2 (.sel(busy), .in_0(B), .in_1(sub_2_s), .out(newB));
  // Probe on newA
  // Probe on newB
  not not_2 (not_2_out, a_gt_b);
  not not_3 (not_3_out, a_eq__eq_b);
  Decoder #(.Selector_Bits(2)) decoder_1 (.sel({Qa, Qb}), .out_0(S00), .out_1(S01), .out_2(S10), .out_3(S11));
  not not_4 (not_4_out, a_eq__eq_b);
  and and_1 (and_1_out, not_2_out, not_3_out);
  Multiplexer #(.Selector_Bits(2)) multiplexer_3 (
    .sel({Qa, Qb}), .in_0(1'b0), .in_1(not_4_out), .in_2(1'b0), .in_3(1'b0), .out(multiplexer_3_out));
  Multiplexer #(.Selector_Bits(2)) multiplexer_4 (
    .sel({Qa, Qb}), .in_0(start), .in_1(and_1_out), .in_2(1'b1), .in_3(1'b1), .out(multiplexer_4_out));
  or or_1 (loadA, S10, S00);
  or or_2 (loadB, S11, S00);
  and and_2 (and_2_out, multiplexer_3_out, clear_t);
  and and_3 (and_3_out, multiplexer_4_out, clear_t);
  not not_5 (busy, S00);
  D_FF d_ff_1 (.D(and_2_out), .C(clk), .Q(Qa));  // open: nQ
  D_FF d_ff_2 (.D(and_3_out), .C(clk), .Q(Qb));  // open: nQ

  // Other names for the same wires on the sheet: loadOut = busy; newOut[7:0] = a_t; out[7:0] = \output ;
  //   State[1:0] = {Qa, Qb}

  // Notes on the sheet:
  //   Assignment
  //   A / B / Out Logic
  //   States
endmodule
