// Digital circuit diglab_08_02.dig as structural Verilog
module diglab_08_02 (
  input  reset,
  input  [15:0] P,
  input  start,
  input  clock,
  output [15:0] W,
  output [15:0] H,
  output [31:0] A,
  output busy
);

  wire and_1_out, and_2_out, decoder_1_out_2, decoder_1_out_3, loadA, loadP, multiplexer_1_out,
       multiplexer_2_out, Q0, Q1, reset_t;
  wire [15:0] floor__W_plus_H__2_r, new_H, new_W, P_t, W_plus_H_q;
  wire [31:0] new_A;

  Register #(.Bits(16)) Reg_P (.D(P), .C(clock), .en(loadP), .Q(P_t));
  Register #(.Bits(16)) Reg_W (.D(new_W), .C(clock), .en(loadA), .Q(W));
  Register #(.Bits(16)) Reg_H (.D(new_H), .C(clock), .en(loadA), .Q(H));
  Register #(.Bits(32)) Reg_A (.D(new_A), .C(clock), .en(loadA), .Q(A));
  // Probe on P_t
  // Probe on W
  // Probe on H
  // Probe on A
  Div #(.Bits(16)) W_plus_H (.a(P_t), .b(16'h2), .q(W_plus_H_q));  // open: r
  Div #(.Bits(16)) floor__W_plus_H__2 (.a(W_plus_H_q), .b(16'h2), .q(new_H), .r(floor__W_plus_H__2_r));
  not not_1 (reset_t, reset);
  Add #(.Bits(16)) u_W (.a(floor__W_plus_H__2_r), .b(new_H), .c_i(1'b0), .s(new_W));  // open: c_o
  Mul #(.Bits(16)) W_H (.a(new_H), .b(new_W), .mul(new_A));
  Multiplexer #(.Selector_Bits(2)) multiplexer_1 (
    .sel({Q1, Q0}), .in_0(1'b0), .in_1(1'b1), .in_2(1'b0), .in_3(1'b0), .out(multiplexer_1_out));
  Multiplexer #(.Selector_Bits(2)) multiplexer_2 (
    .sel({Q1, Q0}), .in_0(start), .in_1(1'b0), .in_2(1'b0), .in_3(1'b0), .out(multiplexer_2_out));
  Decoder #(.Selector_Bits(2)) decoder_1 (
    .sel({Q1, Q0}), .out_0(loadP), .out_1(loadA), .out_2(decoder_1_out_2), .out_3(decoder_1_out_3));
  and and_1 (and_1_out, multiplexer_1_out, reset_t);
  and and_2 (and_2_out, multiplexer_2_out, reset_t);
  not not_2 (busy, loadP);
  D_FF d_ff_1 (.D(and_1_out), .C(clock), .Q(Q1));  // open: nQ
  D_FF d_ff_2 (.D(and_2_out), .C(clock), .Q(Q0));  // open: nQ

  // Other names for the same wires on the sheet: clk = clock; loadH = loadA; loadW = loadA; new_P[15:0] = P;
  //   state[1:0] = {Q1, Q0}
endmodule

/* Test case T01:
P start clock reset W H A busy
0 0 0 1 x x x x
0 0 1 1 x x x x
0 0 0 0 0 0 0 0
0 0 1 0 0 0 0 0
92 1 0 0 x x x x
92 1 1 0 x x x x
0 0 0 0 x x x x
0 0 1 0 x x x x
0 0 0 0 x x x x
0 0 1 0 x x x x
0 0 0 0 x x x x
0 0 1 0 x x x x
0 0 0 0 x x x x
0 0 1 0 x x x x
0 0 0 0 x x x x
0 0 1 0 x x x x
0 0 0 0 x x x x
0 0 1 0 x x x x
0 0 0 0 x x x x
0 0 1 0 x x x x
0 0 0 0 x x x x
0 0 1 0 x x x x
0 0 0 0 x x x x
0 0 1 0 x x x x
0 0 0 0 x x x x
0 0 1 0 x x x x
0 0 0 0 x x x x
0 0 1 0 x x x x
0 0 0 0 x x x x
0 0 1 0 x x x x
0 0 0 0 x x x x
0 0 1 0 x x x x
0 0 0 0 x x x x
0 0 1 0 x x x x
0 0 0 0 x x x x
0 0 1 0 x x x x
0 0 0 0 x x x x
0 0 1 0 x x x x
0 0 0 0 x x x x
0 0 1 0 x x x x
0 0 0 0 x x x x
0 0 1 0 x x x x
0 0 0 0 x x x x
0 0 1 0 x x x x
0 0 0 0 x x x x
0 0 1 0 x x x x
0 0 0 0 x x x x
0 0 1 0 x x x x
0 0 0 0 x x x x
0 0 1 0 x x x x
0 0 0 0 x x x x
0 0 1 0 x x x x
0 0 0 0 x x x x
0 0 1 0 x x x x
0 0 0 0 x x x x
0 0 1 0 x x x x
0 0 0 0 x x x x
0 0 1 0 x x x x
0 0 0 0 x x x x
0 0 1 0 x x x x
0 0 0 0 x x x x
0 0 1 0 x x x x
0 0 0 0 x x x x
0 0 1 0 x x x x
0 0 0 0 x x x x
0 0 1 0 x x x x
0 0 0 0 x x x x
0 0 1 0 x x x x
0 0 0 0 x x x x
0 0 1 0 x x x x
0 0 0 0 x x x x
0 0 1 0 x x x x
0 0 0 0 x x x x
0 0 1 0 x x x x
0 0 0 0 x x x x
0 0 1 0 x x x x
0 0 0 0 x x x x
0 0 1 0 x x x x
0 0 0 0 x x x x
0 0 1 0 x x x x
0 0 0 0 x x x x
0 0 1 0 x x x x
0 0 0 0 x x x x
0 0 1 0 x x x x
0 0 0 0 x x x x
0 0 1 0 x x x x
0 0 0 0 x x x x
0 0 1 0 x x x x
0 0 0 0 x x x x
0 0 1 0 x x x x
0 0 0 0 x x x x
0 0 1 0 x x x x
0 0 0 0 x x x x
0 0 1 0 x x x x
0 0 0 0 x x x x
0 0 1 0 x x x x
0 0 0 0 x x x x
0 0 1 0 x x x x
0 0 0 0 x x x x
0 0 1 0 x x x x
0 0 0 0 x x x x
0 0 1 0 x x x x
0 0 0 0 x x x x
0 0 1 0 x x x x
0 0 0 0 x x x x
0 0 1 0 x x x x
0 0 0 0 x x x x
0 0 1 0 x x x x
0 0 0 0 x x x x
0 0 1 0 x x x x
0 0 0 0 x x x x
0 0 1 0 x x x x
0 0 0 0 x x x x
0 0 1 0 x x x x
0 0 0 0 x x x x
0 0 1 0 x x x x
0 0 0 0 x x x x
0 0 1 0 x x x x
0 0 0 0 x x x x
0 0 1 0 x x x x
0 0 0 0 x x x x
0 0 1 0 x x x x
0 0 0 0 x x x x
0 0 1 0 x x x x
0 0 0 0 x x x x
0 0 1 0 x x x x
0 0 0 0 x x x x
0 0 1 0 x x x x
0 0 0 0 x x x x
0 0 1 0 x x x x
0 0 0 0 x x x x
0 0 1 0 x x x x
0 0 0 0 x x x x
0 0 1 0 x x x x
0 0 0 0 x x x x
0 0 1 0 x x x x
0 0 0 0 x x x x
0 0 1 0 x x x x
0 0 0 0 x x x x
0 0 1 0 x x x x
0 0 0 0 x x x x
0 0 1 0 x x x x
0 0 0 0 x x x x
0 0 1 0 x x x x
0 0 0 0 x x x x
0 0 1 0 x x x x
0 0 0 0 x x x x
0 0 1 0 x x x x
0 0 0 0 x x x x
0 0 1 0 x x x x
0 0 0 0 x x x x
0 0 1 0 x x x x
0 0 0 0 x x x x
0 0 1 0 x x x x
0 0 0 0 x x x x
0 0 1 0 x x x x
0 0 0 0 x x x x
0 0 1 0 x x x x
0 0 0 0 x x x x
0 0 1 0 x x x x
0 0 0 0 x x x x
0 0 1 0 x x x x
0 0 0 0 x x x x
0 0 1 0 x x x x
0 0 0 0 x x x x
0 0 1 0 x x x x
0 0 0 0 x x x x
0 0 1 0 x x x x
0 0 0 0 x x x x
0 0 1 0 x x x x
0 0 0 0 x x x x
0 0 1 0 x x x x
0 0 0 0 x x x x
0 0 1 0 x x x x
0 0 0 0 x x x x
0 0 1 0 x x x x
0 0 0 0 x x x x
0 0 1 0 x x x x
0 0 0 0 x x x x
0 0 1 0 x x x x
0 0 0 0 x x x x
0 0 1 0 x x x x
0 0 0 0 x x x x
0 0 1 0 x x x x
0 0 0 0 x x x x
0 0 1 0 x x x x
0 0 0 0 x x x x
0 0 1 0 x x x x
0 0 0 0 x x x x
0 0 1 0 x x x x
0 0 0 0 x x x x
0 0 1 0 x x x x
0 0 0 0 x x x x
0 0 1 0 x x x x
0 0 0 0 x x x x
0 0 1 0 x x x x
0 0 0 0 x x x x
0 0 1 0 x x x x
0 0 0 0 x x x x
0 0 1 0 x x x x
0 0 0 0 x x x x
0 0 1 0 x x x x
0 0 0 0 x x x x
0 0 1 0 x x x x
0 0 0 0 x x x x
0 0 1 0 x x x x
0 0 0 0 x x x x
0 0 1 0 x x x x
0 0 0 0 x x x x
0 0 1 0 x x x x
0 0 0 0 x x x x
0 0 1 0 x x x x
0 0 0 0 x x x x
0 0 1 0 x x x x
0 0 0 0 x x x x
0 0 1 0 x x x x
0 0 0 0 x x x x
0 0 1 0 x x x x
0 0 0 0 x x x x
0 0 1 0 x x x x
0 0 0 0 x x x x
0 0 1 0 x x x x
0 0 0 0 x x x x
0 0 1 0 x x x x
0 0 0 0 x x x x
0 0 1 0 x x x x
0 0 0 0 x x x x
0 0 1 0 x x x x
0 0 0 0 x x x x
0 0 1 0 x x x x
0 0 0 0 x x x x
0 0 1 0 x x x x
0 0 0 0 x x x x
0 0 1 0 x x x x
0 0 0 0 x x x x
0 0 1 0 x x x x
0 0 0 0 x x x x
0 0 1 0 x x x x
0 0 0 0 x x x x
0 0 1 0 x x x x
0 0 0 0 x x x x
0 0 1 0 x x x x
0 0 0 0 x x x x
0 0 1 0 x x x x
0 0 0 0 x x x x
0 0 1 0 x x x x
0 0 0 0 x x x x
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*/
