// Digital circuit LoyKrathong.dig as structural Verilog
module LoyKrathong (
  input  clk,
  input  clk_2
);

  wire multiplexer_1_out, xor_1_out;

  Multiplexer multiplexer_1 (.sel(clk), .in_0(clk_2), .in_1(xor_1_out), .out(multiplexer_1_out));
  xor xor_1 (xor_1_out, clk, clk_2);

  // Notes on the sheet:
  //   clk_2: Hz: 2
  //   Happy Loy Krathong Day!
endmodule
