// Digital circuit DigLo66_Quiz1__01.dig as structural Verilog
module DigLo66_Quiz1__01 (
  input  [3:0] in,
  output out
);

  Multiplexer #(.Selector_Bits(4)) multiplexer_1 (
    .sel(in), .in_0(1'b0), .in_1(1'b1), .in_2(1'b0), .in_3(1'b1), .in_4(1'b1), .in_5(1'b1), .in_6(1'b0),
    .in_7(1'b0), .in_8(1'b0), .in_9(1'b1), .in_10(1'b1), .in_11(1'b0), .in_12(1'b0), .in_13(1'b1),
    .in_14(1'b1), .in_15(1'b0), .out(out));
endmodule
