// Digital circuit DigLo66_Quiz1__02.dig as structural Verilog
module DigLo66_Quiz1__02 (
  input  [2:0] in1,
  input  [2:0] in0,
  input  addsubtract,
  output [2:0] out
);

  wire [2:0] add_1_s, multiplexer_1_out, multiplexer_2_out, sub_1_s;

  Multiplexer #(.Bits(3), .Selector_Bits(3)) multiplexer_1 (
    .sel(in0), .in_0(3'b000), .in_1(3'b001), .in_2(3'b001), .in_3(3'b010), .in_4(3'b001), .in_5(3'b010),
    .in_6(3'b010), .in_7(3'b011), .out(multiplexer_1_out));
  Multiplexer #(.Selector_Bits(3), .Bits(3)) multiplexer_2 (
    .sel(in1), .in_0(3'b000), .in_1(3'b001), .in_2(3'b001), .in_3(3'b010), .in_4(3'b001), .in_5(3'b010),
    .in_6(3'b010), .in_7(3'b011), .out(multiplexer_2_out));
  Add #(.Bits(3)) add_1 (.a(multiplexer_1_out), .b(multiplexer_2_out), .c_i(1'b0), .s(add_1_s));  // open: c_o
  Sub #(.Bits(3)) sub_1 (.a(multiplexer_1_out), .b(multiplexer_2_out), .c_i(1'b0), .s(sub_1_s));  // open: c_o
  Multiplexer #(.Bits(3)) multiplexer_3 (.sel(addsubtract), .in_0(add_1_s), .in_1(sub_1_s), .out(out));
endmodule
