// Digital circuit DigLo67_Exam1__01.dig as structural Verilog
module DigLo67_Exam1__01 (
  input  X1,
  input  X2,
  input  X3,
  input  X4,
  output Y1,
  output [4:0] CheckGlitch
);

  Multiplexer #(.Selector_Bits(3)) multiplexer_1 (
    .sel({X1, X2, X3}), .in_0(1'b0), .in_1(1'b0), .in_2(1'b0), .in_3(X4), .in_4(1'b1), .in_5(1'b0),
    .in_6(1'b1), .in_7(X4), .out(Y1));
  Counter #(.Bits(5)) counter_1 (.en(1'b1), .C(Y1), .clr(1'b0), .out(CheckGlitch));  // open: ovf

  // Notes on the sheet:
  //   Must not change this section
endmodule
