// Digital circuit DigLo67_Exam1__02.dig as structural Verilog
module DigLo67_Exam1__02 (
  input  [1:0] X,
  input  [1:0] Y,
  output [4:0] Z
);

  Multiplexer #(.Bits(5), .Selector_Bits(4)) multiplexer_1 (
    .sel({X, Y}), .in_0(5'b00001), .in_1({5{1'b0}}), .in_2({5{1'b0}}), .in_3({5{1'b0}}), .in_4(5'b00001),
    .in_5(5'b00001), .in_6(5'b00001), .in_7(5'b00001), .in_8(5'b00001), .in_9(5'b00010), .in_10(5'b01000),
    .in_11(5'b10000), .in_12(5'b00001), .in_13(5'b00011), .in_14(5'b01001), .in_15(5'b11011), .out(Z));
endmodule
