// Digital circuit DigLo67_Exam1__03.dig as structural Verilog
module DigLo67_Exam1__03 (
  input  [2:0] A,
  input  [3:0] B,
  output out_3
);

  wire comparator_1_gt, comparator_2_gt;
  wire [1:0] bitcount_1_out;
  wire [2:0] bitcount_2_out;

  BitCount #(.Bits(3)) bitcount_1 (.in(A), .out(bitcount_1_out));
  BitCount #(.Bits(4)) bitcount_2 (.in(B), .out(bitcount_2_out));
  Comparator #(.Bits(2)) comparator_1 (.a(bitcount_1_out), .b(2'b01), .gt(comparator_1_gt));  // open: eq, lt
  Comparator #(.Bits(3)) comparator_2 (.a(bitcount_2_out), .b(3'b001), .gt(comparator_2_gt));  // open: eq, lt
  or or_1 (out_3, comparator_1_gt, comparator_2_gt);
endmodule
