// Digital circuit DigLo67_Exam3__03.dig as structural Verilog
module DigLo67_Exam3__03 (
  input  reset,
  input  [7:0] N,
  input  \new ,
  input  clock,
  output [7:0] num_inc,
  output [7:0] max,
  output busy
);

  wire and_1_out, and_2_out, decoder_1_out_2, decoder_1_out_3, loadAns, loadN, multiplexer_1_out,
       multiplexer_2_out, multiplexer_7_out, multiplexer_8_out, N__gt__max_gt, reset_t, S0, S1;
  wire [7:0] multiplexer_3_out, multiplexer_4_out, Mx_new, N_t, num_inc_plus__plus_s, NumInc_new;

  Multiplexer multiplexer_1 (.sel(reset_t), .in_0(1'b1), .in_1(loadAns), .out(multiplexer_1_out));
  Multiplexer multiplexer_2 (.sel(reset_t), .in_0(1'b1), .in_1(loadAns), .out(multiplexer_2_out));
  Multiplexer #(.Bits(8)) multiplexer_3 (.sel(reset_t), .in_0({8{1'b0}}), .in_1(NumInc_new), .out(multiplexer_3_out));
  Multiplexer #(.Bits(8)) multiplexer_4 (.sel(reset_t), .in_0({8{1'b0}}), .in_1(Mx_new), .out(multiplexer_4_out));
  Register #(.Bits(8)) u_N (.D(N), .C(clock), .en(loadN), .Q(N_t));
  Register #(.Bits(8)) u_num_inc (.D(multiplexer_3_out), .C(clock), .en(multiplexer_2_out), .Q(num_inc));
  Register #(.Bits(8)) Mx (.D(multiplexer_4_out), .C(clock), .en(multiplexer_1_out), .Q(max));
  // Probe on N_t
  // Probe on num_inc
  // Probe on max
  not not_1 (reset_t, reset);
  Comparator #(.Bits(8)) N__gt__max (.a(N_t), .b(max), .gt(N__gt__max_gt));  // open: eq, lt
  Add #(.Bits(8)) num_inc_plus__plus (.a(8'h1), .b(num_inc), .c_i(1'b0), .s(num_inc_plus__plus_s));  // open: c_o
  Multiplexer #(.Bits(8)) multiplexer_5 (.sel(N__gt__max_gt), .in_0(max), .in_1(N_t), .out(Mx_new));
  Multiplexer #(.Bits(8)) multiplexer_6 (
    .sel(N__gt__max_gt), .in_0(num_inc), .in_1(num_inc_plus__plus_s), .out(NumInc_new));
  Multiplexer #(.Selector_Bits(2)) multiplexer_7 (
    .sel({S1, S0}), .in_0(1'b0), .in_1(1'b0), .in_2(1'b0), .in_3(1'b0), .out(multiplexer_7_out));
  Multiplexer #(.Selector_Bits(2)) multiplexer_8 (
    .sel({S1, S0}), .in_0(\new ), .in_1(1'b0), .in_2(1'b0), .in_3(1'b0), .out(multiplexer_8_out));
  Decoder #(.Selector_Bits(2)) decoder_1 (
    .sel({S1, S0}), .out_0(loadN), .out_1(loadAns), .out_2(decoder_1_out_2), .out_3(decoder_1_out_3));
  not not_2 (busy, loadN);
  and and_1 (and_1_out, multiplexer_7_out, reset_t);
  and and_2 (and_2_out, multiplexer_8_out, reset_t);
  D_FF d_ff_1 (.D(and_1_out), .C(clock), .Q(S1));  // open: nQ
  D_FF d_ff_2 (.D(and_2_out), .C(clock), .Q(S0));  // open: nQ

  // Other names for the same wires on the sheet: clk = clock; N_new[7:0] = N; state[1:0] = {S1, S0}
endmodule

/* Test case T06:
N new reset clock num_inc max busy
0 0 1 0 x x x
0 0 1 1 0 0 0
131 1 0 0 x x x
131 1 0 1 x x x
0 0 0 0 x x x
0 0 0 1 x x x
0 0 0 0 x x x
0 0 0 1 x x x
0 0 0 0 x x x
0 0 0 1 x x x
0 0 0 0 x x x
0 0 0 1 x x x
0 0 0 0 x x x
0 0 0 1 x x x
0 0 0 0 x x x
0 0 0 1 x x x
0 0 0 0 x x x
0 0 0 1 x x x
0 0 0 0 x x x
0 0 0 1 x x x
0 0 0 0 x x x
0 0 0 1 x x x
0 0 0 0 x x x
0 0 0 1 x x x
0 0 0 0 x x x
0 0 0 1 x x x
0 0 0 0 x x x
0 0 0 1 x x x
0 0 0 0 x x x
0 0 0 1 x x x
0 0 0 0 x x x
0 0 0 1 x x x
0 0 0 0 x x x
0 0 0 1 x x x
0 0 0 0 x x x
0 0 0 1 x x x
0 0 0 0 x x x
0 0 0 1 x x x
0 0 0 0 x x x
0 0 0 1 x x x
0 0 0 0 x x x
0 0 0 1 x x x
0 0 0 0 x x x
0 0 0 1 x x x
0 0 0 0 x x x
0 0 0 1 x x x
0 0 0 0 x x x
0 0 0 1 x x x
0 0 0 0 x x x
0 0 0 1 x x x
0 0 0 0 x x x
0 0 0 1 x x x
0 0 0 0 x x x
0 0 0 1 x x x
0 0 0 0 x x x
0 0 0 1 x x x
0 0 0 0 x x x
0 0 0 1 x x x
0 0 0 0 x x x
0 0 0 1 x x x
0 0 0 0 x x x
0 0 0 1 x x x
0 0 0 0 x x x
0 0 0 1 x x x
0 0 0 0 1 131 0
0 0 0 1 1 131 0
130 1 0 0 x x x
130 1 0 1 x x x
0 0 0 0 x x x
0 0 0 1 x x x
0 0 0 0 x x x
0 0 0 1 x x x
0 0 0 0 x x x
0 0 0 1 x x x
0 0 0 0 x x x
0 0 0 1 x x x
0 0 0 0 x x x
0 0 0 1 x x x
0 0 0 0 x x x
0 0 0 1 x x x
0 0 0 0 x x x
0 0 0 1 x x x
0 0 0 0 x x x
0 0 0 1 x x x
0 0 0 0 x x x
0 0 0 1 x x x
0 0 0 0 x x x
0 0 0 1 x x x
0 0 0 0 x x x
0 0 0 1 x x x
0 0 0 0 x x x
0 0 0 1 x x x
0 0 0 0 x x x
0 0 0 1 x x x
0 0 0 0 x x x
0 0 0 1 x x x
0 0 0 0 x x x
0 0 0 1 x x x
0 0 0 0 x x x
0 0 0 1 x x x
0 0 0 0 x x x
0 0 0 1 x x x
0 0 0 0 x x x
0 0 0 1 x x x
0 0 0 0 x x x
0 0 0 1 x x x
0 0 0 0 x x x
0 0 0 1 x x x
0 0 0 0 x x x
0 0 0 1 x x x
0 0 0 0 x x x
0 0 0 1 x x x
0 0 0 0 x x x
0 0 0 1 x x x
0 0 0 0 x x x
0 0 0 1 x x x
0 0 0 0 x x x
0 0 0 1 x x x
0 0 0 0 x x x
0 0 0 1 x x x
0 0 0 0 x x x
0 0 0 1 x x x
0 0 0 0 x x x
0 0 0 1 x x x
0 0 0 0 x x x
0 0 0 1 x x x
0 0 0 0 x x x
0 0 0 1 x x x
0 0 0 0 1 131 0
0 0 0 1 1 131 0
58 1 0 0 x x x
58 1 0 1 x x x
0 0 0 0 x x x
0 0 0 1 x x x
0 0 0 0 x x x
0 0 0 1 x x x
0 0 0 0 x x x
0 0 0 1 x x x
0 0 0 0 x x x
0 0 0 1 x x x
0 0 0 0 x x x
0 0 0 1 x x x
0 0 0 0 x x x
0 0 0 1 x x x
0 0 0 0 x x x
0 0 0 1 x x x
0 0 0 0 x x x
0 0 0 1 x x x
0 0 0 0 x x x
0 0 0 1 x x x
0 0 0 0 x x x
0 0 0 1 x x x
0 0 0 0 x x x
0 0 0 1 x x x
0 0 0 0 x x x
0 0 0 1 x x x
0 0 0 0 x x x
0 0 0 1 x x x
0 0 0 0 x x x
0 0 0 1 x x x
0 0 0 0 x x x
0 0 0 1 x x x
0 0 0 0 x x x
0 0 0 1 x x x
0 0 0 0 x x x
0 0 0 1 x x x
0 0 0 0 x x x
0 0 0 1 x x x
0 0 0 0 x x x
0 0 0 1 x x x
0 0 0 0 x x x
0 0 0 1 x x x
0 0 0 0 x x x
0 0 0 1 x x x
0 0 0 0 x x x
0 0 0 1 x x x
0 0 0 0 x x x
0 0 0 1 x x x
0 0 0 0 x x x
0 0 0 1 x x x
0 0 0 0 x x x
0 0 0 1 x x x
0 0 0 0 x x x
0 0 0 1 x x x
0 0 0 0 x x x
0 0 0 1 x x x
0 0 0 0 x x x
0 0 0 1 x x x
0 0 0 0 x x x
0 0 0 1 x x x
0 0 0 0 x x x
0 0 0 1 x x x
0 0 0 0 1 131 0
0 0 0 1 1 131 0
154 1 0 0 x x x
154 1 0 1 x x x
0 0 0 0 x x x
0 0 0 1 x x x
0 0 0 0 x x x
0 0 0 1 x x x
0 0 0 0 x x x
0 0 0 1 x x x
0 0 0 0 x x x
0 0 0 1 x x x
0 0 0 0 x x x
0 0 0 1 x x x
0 0 0 0 x x x
0 0 0 1 x x x
0 0 0 0 x x x
0 0 0 1 x x x
0 0 0 0 x x x
0 0 0 1 x x x
0 0 0 0 x x x
0 0 0 1 x x x
0 0 0 0 x x x
0 0 0 1 x x x
0 0 0 0 x x x
0 0 0 1 x x x
0 0 0 0 x x x
0 0 0 1 x x x
0 0 0 0 x x x
0 0 0 1 x x x
0 0 0 0 x x x
0 0 0 1 x x x
0 0 0 0 x x x
0 0 0 1 x x x
0 0 0 0 x x x
0 0 0 1 x x x
0 0 0 0 x x x
0 0 0 1 x x x
0 0 0 0 x x x
0 0 0 1 x x x
0 0 0 0 x x x
0 0 0 1 x x x
0 0 0 0 x x x
0 0 0 1 x x x
0 0 0 0 x x x
0 0 0 1 x x x
0 0 0 0 x x x
0 0 0 1 x x x
0 0 0 0 x x x
0 0 0 1 x x x
0 0 0 0 x x x
0 0 0 1 x x x
0 0 0 0 x x x
0 0 0 1 x x x
0 0 0 0 x x x
0 0 0 1 x x x
0 0 0 0 x x x
0 0 0 1 x x x
0 0 0 0 x x x
0 0 0 1 x x x
0 0 0 0 x x x
0 0 0 1 x x x
0 0 0 0 x x x
0 0 0 1 x x x
0 0 0 0 2 154 0
0 0 0 1 2 154 0
122 1 0 0 x x x
122 1 0 1 x x x
0 0 0 0 x x x
0 0 0 1 x x x
0 0 0 0 x x x
0 0 0 1 x x x
0 0 0 0 x x x
0 0 0 1 x x x
0 0 0 0 x x x
0 0 0 1 x x x
0 0 0 0 x x x
0 0 0 1 x x x
0 0 0 0 x x x
0 0 0 1 x x x
0 0 0 0 x x x
0 0 0 1 x x x
0 0 0 0 x x x
0 0 0 1 x x x
0 0 0 0 x x x
0 0 0 1 x x x
0 0 0 0 x x x
0 0 0 1 x x x
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*/
