// Digital circuit DigLo68_Exam1__02.dig as structural Verilog
module DigLo68_Exam1__02 (
  input  X3,
  input  X2,
  input  X1,
  input  X0,
  output Z3,
  output Z2,
  output Z1,
  output Z0
);

  wire not_1_out, not_2_out, not_3_out;

  not not_1 (not_1_out, X3);
  not not_2 (not_2_out, X2);
  not not_3 (not_3_out, X1);
  not not_4 (Z2, X0);
  Multiplexer #(.Selector_Bits(4)) multiplexer_1 (
    .sel({X3, X2, X1, X0}), .in_0(1'b0), .in_1(1'b0), .in_2(1'b1), .in_3(1'b1), .in_4(1'b0), .in_5(1'b1),
    .in_6(1'b0), .in_7(1'b1), .in_8(1'b0), .in_9(1'b0), .in_10(1'b0), .in_11(1'b1), .in_12(1'b0),
    .in_13(1'b1), .in_14(1'b0), .in_15(1'b0), .out(Z3));
  Multiplexer #(.Selector_Bits(4)) multiplexer_2 (
    .sel({X3, X2, X1, X0}), .in_0(1'b1), .in_1(1'b0), .in_2(1'b0), .in_3(1'b1), .in_4(1'b0), .in_5(1'b0),
    .in_6(1'b1), .in_7(1'b0), .in_8(1'b0), .in_9(1'b1), .in_10(1'b0), .in_11(1'b0), .in_12(1'b1),
    .in_13(1'b0), .in_14(1'b0), .in_15(1'b1), .out(Z1));
  Multiplexer #(.Selector_Bits(4)) multiplexer_3 (
    .sel({X3, X2, X1, X0}), .in_0(1'b1), .in_1(1'b0), .in_2(1'b0), .in_3(1'b0), .in_4(1'b0), .in_5(1'b1),
    .in_6(1'b0), .in_7(1'b0), .in_8(1'b0), .in_9(1'b0), .in_10(1'b1), .in_11(1'b0), .in_12(1'b0),
    .in_13(1'b0), .in_14(1'b0), .in_15(1'b1), .out(Z0));

  // Notes on the sheet:
  //   Z3: Is prime number?
  //   Z2: Is it divisible by 2?
  //   Z1: Is it divisible by 3?
  //   Z0: Is it divisible by 5?
  //   Don't change anything inside this box
endmodule

/* Test case T1:
X3 X2 X1 X0 Z3 Z2 Z1 Z0
0 0 0 0 0 1 1 1
0 1 1 1 1 0 0 0
1 0 1 0 0 1 0 1
*/
