// Digital circuit DigLo68_Exam2__01.dig as structural Verilog
module DigLo68_Exam2__01 (
  input  reset,
  input  X,
  input  Y,
  input  Z,
  input  load,
  input  clock,
  output A,
  output B,
  output C
);

  wire newA, newB, newC;
  wire [2:0] multiplexer_1_out, multiplexer_2_out;

  D_FF d_ff_1 (.D(newA), .C(clock), .Q(A));  // open: nQ
  D_FF d_ff_2 (.D(newB), .C(clock), .Q(B));  // open: nQ
  D_FF d_ff_3 (.D(newC), .C(clock), .Q(C));  // open: nQ
  Multiplexer #(.Bits(3), .Selector_Bits(3)) multiplexer_1 (
    .sel({A, B, C}), .in_0(3'b111), .in_1(3'b111), .in_2(3'b110), .in_3(3'b000), .in_4(3'b010),
    .in_5(3'b110), .in_6(3'b011), .in_7(3'b100), .out(multiplexer_1_out));
  Multiplexer #(.Bits(3)) multiplexer_2 (
    .sel(load), .in_0(multiplexer_1_out), .in_1({X, Y, Z}), .out(multiplexer_2_out));
  Multiplexer #(.Bits(3)) multiplexer_3 (
    .sel(reset), .in_0(multiplexer_2_out), .in_1(3'b010), .out({newA, newB, newC}));

  // Other names for the same wires on the sheet: clk = clock
endmodule

/* Test case T01:
X Y Z reset load clock A B C
0 0 0 1 0 0 x x x
0 0 0 1 0 1 0 0 0
1 1 0 0 1 0 0 0 0
1 1 0 0 1 1 1 1 0
0 0 0 0 0 0 1 1 0
0 0 0 0 0 1 0 1 1
0 0 0 0 0 0 0 1 1
0 0 0 0 0 1 0 0 0
0 0 0 0 0 0 0 0 0
0 0 0 0 0 1 1 1 1
0 0 0 0 0 0 1 1 1
0 0 0 0 0 1 1 0 0
0 0 0 0 0 0 1 0 0
0 0 0 0 0 1 0 1 0
0 0 0 0 0 0 0 1 0
0 0 0 0 0 1 1 1 0
0 0 0 0 0 0 1 1 0
0 0 0 0 0 1 0 1 1
0 0 0 0 0 0 0 1 1
0 0 0 0 0 1 0 0 0
0 0 0 0 0 0 0 0 0
*/
