// Digital circuit DigLo68_Exam2__02.dig as structural Verilog
module DigLo68_Exam2__02 (
  input  reset,
  input  [7:0] M,
  input  start,
  input  clock,
  input  [7:0] N,
  output [15:0] Z,
  output busy
);

  wire and_1_out, and_2_out, and_3_out, and_4_out, comparator_1_eq, comparator_1_lt, comparator_2_lt,
       decoder_1_out_2, decoder_1_out_3, loadM, loadN, loadSum, multiplexer_4_out, multiplexer_10_out,
       multiplexer_11_out, not_1_out, not_2_out, not_3_out, not_4_out, or_1_out, S0, S1;
  wire [7:0] M_plus__eq_2_s, M_plus__plus_s, M_t, multiplexer_1_out, multiplexer_2_out, multiplexer_5_out,
       multiplexer_6_out, N_t, newM, newN;
  wire [15:0] multiplexer_3_out, newSum, Z_plus__eq_M_s;

  Multiplexer #(.Bits(8)) multiplexer_1 (.sel(reset), .in_0(newM), .in_1({8{1'b0}}), .out(multiplexer_1_out));
  Multiplexer #(.Bits(8)) multiplexer_2 (.sel(reset), .in_0(newN), .in_1({8{1'b0}}), .out(multiplexer_2_out));
  Multiplexer #(.Bits(16)) multiplexer_3 (.sel(reset), .in_0(newSum), .in_1({16{1'b0}}), .out(multiplexer_3_out));
  Multiplexer multiplexer_4 (.sel(reset), .in_0(loadSum), .in_1(1'b1), .out(multiplexer_4_out));
  Register #(.Bits(8)) u_M (.D(multiplexer_1_out), .C(clock), .en(loadM), .Q(M_t));
  Register #(.Bits(8)) u_N (.D(multiplexer_2_out), .C(clock), .en(loadN), .Q(N_t));
  Register #(.Bits(16)) Sum (.D(multiplexer_3_out), .C(clock), .en(multiplexer_4_out), .Q(Z));
  // Probe on M_t
  // Probe on N_t
  // Probe on Z
  Add #(.Bits(16)) Z_plus__eq_M (.a({{8{1'b0}}, M_t}), .b(Z), .c_i(1'b0), .s(Z_plus__eq_M_s));  // open: c_o
  Add #(.Bits(8)) M_plus__plus (.a(M_t), .b(8'h1), .c_i(1'b0), .s(M_plus__plus_s));  // open: c_o
  Add #(.Bits(8)) M_plus__eq_2 (.a(M_t), .b(8'h2), .c_i(1'b0), .s(M_plus__eq_2_s));  // open: c_o
  not not_1 (not_1_out, M_t[0]);
  Multiplexer #(.Bits(8)) multiplexer_5 (.sel(busy), .in_0(M), .in_1(M_plus__plus_s), .out(multiplexer_5_out));
  Multiplexer #(.Bits(8)) multiplexer_6 (.sel(busy), .in_0(M), .in_1(M_plus__eq_2_s), .out(multiplexer_6_out));
  not not_2 (not_2_out, M_t[0]);
  Multiplexer #(.Bits(8)) multiplexer_7 (.sel(busy), .in_0(N), .in_1(N_t), .out(newN));
  Multiplexer #(.Bits(16)) multiplexer_8 (.sel(not_1_out), .in_0(Z), .in_1(Z_plus__eq_M_s), .out(newSum));
  Multiplexer #(.Bits(8)) multiplexer_9 (
    .sel(not_2_out), .in_0(multiplexer_5_out), .in_1(multiplexer_6_out), .out(newM));
  Comparator #(.Bits(8)) comparator_1 (.a(M_t), .b(N_t), .eq(comparator_1_eq), .lt(comparator_1_lt));  // open: gt
  or or_1 (or_1_out, comparator_1_eq, comparator_1_lt);
  Comparator #(.Bits(8)) comparator_2 (.a(M_t), .b(8'hfe), .lt(comparator_2_lt));  // open: gt, eq
  and and_1 (and_1_out, start, or_1_out);
  and and_2 (and_2_out, or_1_out, comparator_2_lt);
  Multiplexer #(.Selector_Bits(2)) multiplexer_10 (
    .sel({S1, S0}), .in_0(1'b0), .in_1(1'b1), .in_2(1'b1), .in_3(1'b0), .out(multiplexer_10_out));
  Multiplexer #(.Selector_Bits(2)) multiplexer_11 (
    .sel({S1, S0}), .in_0(and_1_out), .in_1(1'b0), .in_2(1'b1), .in_3(and_2_out), .out(multiplexer_11_out));
  Decoder #(.Selector_Bits(2)) decoder_1 (
    .sel({S1, S0}), .out_0(loadN), .out_1(loadSum), .out_2(decoder_1_out_2), .out_3(decoder_1_out_3));
  or or_2 (loadM, decoder_1_out_2, loadN);
  not not_3 (not_3_out, reset);
  not not_4 (not_4_out, reset);
  not not_5 (busy, loadN);
  and and_3 (and_3_out, multiplexer_10_out, not_3_out);
  and and_4 (and_4_out, multiplexer_11_out, not_4_out);
  D_FF u_S1 (.D(and_3_out), .C(clock), .Q(S1));  // open: nQ
  D_FF u_S0 (.D(and_4_out), .C(clock), .Q(S0));  // open: nQ

  // Other names for the same wires on the sheet: clk = clock; inM[7:0] = M; inN[7:0] = N; state[1:0] = {S1, S0}
endmodule

/* Test case T01:
 M  N start clock reset Z busy
 0  0 0     0     1     x x
 0  0 0     1     1     x 0
 0  0 0     0     1     x 0
 0  0 0     1     1     x 0
 1 10 1     0     0     x 0
 1 10 1     1     0     x 1
 0  0 0     0     0     x 1
 0  0 0     1     0     x 1
 0  0 0     0     0     x 1
 0  0 0     1     0     x 1
 0  0 0     0     0     x 1
 0  0 0     1     0     x x
 0  0 0     0     0     x x
 0  0 0     1     0     x x
 0  0 0     0     0     x x
 0  0 0     1     0     x x
 0  0 0     0     0     x x
 0  0 0     1     0     x x
 0  0 0     0     0     x x
 0  0 0     1     0     x x
 0  0 0     0     0     x x
 0  0 0     1     0     x x
 0  0 0     0     0     x x
 0  0 0     1     0     x x
 0  0 0     0     0     x x
 0  0 0     1     0     x x
 0  0 0     0     0     x x
 0  0 0     1     0     x x
 0  0 0     0     0     x x
 0  0 0     1     0     x x
 0  0 0     0     0     x x
 0  0 0     1     0     x x
 0  0 0     0     0     x x
 0  0 0     1     0     x x
 0  0 0     0     0     x x
 0  0 0     1     0     x x
 0  0 0     0     0     x x
 0  0 0     1     0     x x
 0  0 0     0     0     x x
 0  0 0     1     0     x x
 0  0 0     0     0     x x
 0  0 0     1     0     x x
 0  0 0     0     0     x x
 0  0 0     1     0     x x
 0  0 0     0     0     x x
 0  0 0     1     0     x x
 0  0 0     0     0     x x
 0  0 0     1     0     x x
 0  0 0     0     0     x x
 0  0 0     1     0     x x
 0  0 0     0     0     x x
 0  0 0     1     0     x x
 0  0 0     0     0     x x
 0  0 0     1     0     x x
 0  0 0     0     0     x x
 0  0 0     1     0     x x
 0  0 0     0     0     x x
 0  0 0     1     0     x x
 0  0 0     0     0     x x
 0  0 0     1     0     x x
 0  0 0     0     0     x x
 0  0 0     1     0     x x
 0  0 0     0     0     x x
 0  0 0     1     0     x x
 0  0 0     0     0     x x
 0  0 0     1     0     x x
 0  0 0     0     0     x x
 0  0 0     1     0     x x
 0  0 0     0     0     x x
 0  0 0     1     0     x x
 0  0 0     0     0     x x
 0  0 0     1     0     x x
 0  0 0     0     0     x x
 0  0 0     1     0     x x
 0  0 0     0     0     x x
 0  0 0     1     0     x x
 0  0 0     0     0     x x
 0  0 0     1     0     x x
 0  0 0     0     0     x x
 0  0 0     1     0     x x
 0  0 0     0     0     x x
 0  0 0     1     0     x x
 0  0 0     0     0     x x
 0  0 0     1     0     x x
 0  0 0     0     0     x x
 0  0 0     1     0     x x
 0  0 0     0     0     x x
 0  0 0     1     0     x x
 0  0 0     0     0     x x
 0  0 0     1     0     x x
 0  0 0     0     0     x x
 0  0 0     1     0     x x
 0  0 0     0     0     x x
 0  0 0     1     0     x x
 0  0 0     0     0     x x
 0  0 0     1     0     x x
 0  0 0     0     0     x x
 0  0 0     1     0     x x
 0  0 0     0     0     x x
 0  0 0     1     0     x x
 0  0 0     0     0     x x
 0  0 0     1     0     x x
 0  0 0     0     0     x x
 0  0 0     1     0     x x
 0  0 0     0     0     x x
 0  0 0     1     0     x x
 0  0 0     0     0     x x
 0  0 0     1     0     x x
 0  0 0     0     0     x x
 0  0 0     1     0     x x
 0  0 0     0     0     x x
 0  0 0     1     0     x x
 0  0 0     0     0     x x
 0  0 0     1     0     x x
 0  0 0     0     0     30 0
 0  0 0     1     0     30 0
 0  0 0     0     0     30 0
 0  0 0     1     0     30 0
*/
