// Digital circuit DigLo68_Exam2__02_V2.dig as structural Verilog
module DigLo68_Exam2__02_V2 (
  input  reset,
  input  [7:0] M,
  input  start,
  input  clock,
  input  [7:0] N,
  output [15:0] Z,
  output busy
);

  wire and_1_out, and_2_out, decoder_1_out_2, decoder_1_out_3, loadM, loadN, loadSum, multiplexer_4_out,
       multiplexer_6_out, multiplexer_7_out, not_1_out, not_2_out, S0, S1;
  wire [7:0] add_1_s, M_t, multiplexer_1_out, multiplexer_2_out, N_t, newM, newN;
  wire [15:0] multiplexer_3_out, newSum;

  Multiplexer #(.Bits(8)) multiplexer_1 (.sel(reset), .in_0(newM), .in_1({8{1'b0}}), .out(multiplexer_1_out));
  Multiplexer #(.Bits(8)) multiplexer_2 (.sel(reset), .in_0(newN), .in_1({8{1'b0}}), .out(multiplexer_2_out));
  Multiplexer #(.Bits(16)) multiplexer_3 (.sel(reset), .in_0(newSum), .in_1({16{1'b0}}), .out(multiplexer_3_out));
  Multiplexer multiplexer_4 (.sel(reset), .in_0(loadSum), .in_1(1'b1), .out(multiplexer_4_out));
  Register #(.Bits(8)) u_M (.D(multiplexer_1_out), .C(clock), .en(loadM), .Q(M_t));
  Register #(.Bits(8)) u_N (.D(multiplexer_2_out), .C(clock), .en(loadN), .Q(N_t));
  Register #(.Bits(16)) Sum (.D(multiplexer_3_out), .C(clock), .en(multiplexer_4_out), .Q(Z));
  // Probe on M_t
  // Probe on N_t
  // Probe on Z
  Add #(.Bits(8)) add_1 (.a(M_t), .b(N_t), .s(add_1_s));  // open: c_i, c_o
  Add #(.Bits(8)) add_2 (.a(M_t), .b(N_t));  // open: c_i, s, c_o
  Multiplexer #(.Bits(8)) multiplexer_5 (.sel(busy), .in_0(N), .in_1(N_t), .out(newN));
  Mul mul_1 (.a(add_1_s[0]));  // open: b, mul
  Multiplexer #(.Selector_Bits(2)) multiplexer_6 (
    .sel({S1, S0}), .in_0(1'b0), .in_1(1'b0), .in_2(1'b0), .in_3(1'b0), .out(multiplexer_6_out));
  Multiplexer #(.Selector_Bits(2)) multiplexer_7 (
    .sel({S1, S0}), .in_0(start), .in_1(1'b0), .in_2(1'b0), .in_3(1'b0), .out(multiplexer_7_out));
  Decoder #(.Selector_Bits(2)) decoder_1 (
    .sel({S1, S0}), .out_0(loadN), .out_1(loadSum), .out_2(decoder_1_out_2), .out_3(decoder_1_out_3));
  or or_1 (loadM, decoder_1_out_3, decoder_1_out_2, loadN);
  not not_1 (not_1_out, reset);
  not not_2 (not_2_out, reset);
  not not_3 (busy, loadN);
  and and_1 (and_1_out, multiplexer_6_out, not_1_out);
  and and_2 (and_2_out, multiplexer_7_out, not_2_out);
  D_FF u_S1 (.D(and_1_out), .C(clock), .Q(S1));  // open: nQ
  D_FF u_S0 (.D(and_2_out), .C(clock), .Q(S0));  // open: nQ
  // Pins of 1 and 8 bits meet at add_1_s

  // Other names for the same wires on the sheet: clk = clock; inM[7:0] = M; inN[7:0] = N; state[1:0] = {S1, S0}
endmodule

/* Test case T01:
 M  N start clock reset Z busy
 0  0 0     0     1     x x
 0  0 0     1     1     x 0
 0  0 0     0     1     x 0
 0  0 0     1     1     x 0
 1 10 1     0     0     x 0
 1 10 1     1     0     x 1
 0  0 0     0     0     x 1
 0  0 0     1     0     x 1
 0  0 0     0     0     x 1
 0  0 0     1     0     x 1
 0  0 0     0     0     x 1
 0  0 0     1     0     x x
 0  0 0     0     0     x x
 0  0 0     1     0     x x
 0  0 0     0     0     x x
 0  0 0     1     0     x x
 0  0 0     0     0     x x
 0  0 0     1     0     x x
 0  0 0     0     0     x x
 0  0 0     1     0     x x
 0  0 0     0     0     x x
 0  0 0     1     0     x x
 0  0 0     0     0     x x
 0  0 0     1     0     x x
 0  0 0     0     0     x x
 0  0 0     1     0     x x
 0  0 0     0     0     x x
 0  0 0     1     0     x x
 0  0 0     0     0     x x
 0  0 0     1     0     x x
 0  0 0     0     0     x x
 0  0 0     1     0     x x
 0  0 0     0     0     x x
 0  0 0     1     0     x x
 0  0 0     0     0     x x
 0  0 0     1     0     x x
 0  0 0     0     0     x x
 0  0 0     1     0     x x
 0  0 0     0     0     x x
 0  0 0     1     0     x x
 0  0 0     0     0     x x
 0  0 0     1     0     x x
 0  0 0     0     0     x x
 0  0 0     1     0     x x
 0  0 0     0     0     x x
 0  0 0     1     0     x x
 0  0 0     0     0     x x
 0  0 0     1     0     x x
 0  0 0     0     0     x x
 0  0 0     1     0     x x
 0  0 0     0     0     x x
 0  0 0     1     0     x x
 0  0 0     0     0     x x
 0  0 0     1     0     x x
 0  0 0     0     0     x x
 0  0 0     1     0     x x
 0  0 0     0     0     x x
 0  0 0     1     0     x x
 0  0 0     0     0     x x
 0  0 0     1     0     x x
 0  0 0     0     0     x x
 0  0 0     1     0     x x
 0  0 0     0     0     x x
 0  0 0     1     0     x x
 0  0 0     0     0     x x
 0  0 0     1     0     x x
 0  0 0     0     0     x x
 0  0 0     1     0     x x
 0  0 0     0     0     x x
 0  0 0     1     0     x x
 0  0 0     0     0     x x
 0  0 0     1     0     x x
 0  0 0     0     0     x x
 0  0 0     1     0     x x
 0  0 0     0     0     x x
 0  0 0     1     0     x x
 0  0 0     0     0     x x
 0  0 0     1     0     x x
 0  0 0     0     0     x x
 0  0 0     1     0     x x
 0  0 0     0     0     x x
 0  0 0     1     0     x x
 0  0 0     0     0     x x
 0  0 0     1     0     x x
 0  0 0     0     0     x x
 0  0 0     1     0     x x
 0  0 0     0     0     x x
 0  0 0     1     0     x x
 0  0 0     0     0     x x
 0  0 0     1     0     x x
 0  0 0     0     0     x x
 0  0 0     1     0     x x
 0  0 0     0     0     x x
 0  0 0     1     0     x x
 0  0 0     0     0     x x
 0  0 0     1     0     x x
 0  0 0     0     0     x x
 0  0 0     1     0     x x
 0  0 0     0     0     x x
 0  0 0     1     0     x x
 0  0 0     0     0     x x
 0  0 0     1     0     x x
 0  0 0     0     0     x x
 0  0 0     1     0     x x
 0  0 0     0     0     x x
 0  0 0     1     0     x x
 0  0 0     0     0     x x
 0  0 0     1     0     x x
 0  0 0     0     0     x x
 0  0 0     1     0     x x
 0  0 0     0     0     x x
 0  0 0     1     0     x x
 0  0 0     0     0     x x
 0  0 0     1     0     x x
 0  0 0     0     0     30 0
 0  0 0     1     0     30 0
 0  0 0     0     0     30 0
 0  0 0     1     0     30 0
*/
