// Digital circuit DigLo68_Exam2__03.dig as structural Verilog
module DigLo68_Exam2__03 (
  input  reset,
  input  [3:0] N,
  input  \new ,
  input  clock,
  output [7:0] num3,
  output [7:0] num5,
  output busy
);

  wire and_1_out, and_2_out, comparator_1_gt, comparator_2_gt, decoder_1_out_0, decoder_1_out_2,
       decoder_1_out_3, loadNum3, multiplexer_2_out, multiplexer_4_out, multiplexer_7_out, multiplexer_8_out,
       not_2_out, not_3_out, S0, S1;
  wire [3:0] div_1_r, div_2_r, N_t;
  wire [7:0] add_1_s, add_2_s, multiplexer_1_out, multiplexer_3_out, newNum3, newNum5;

  Multiplexer #(.Bits(8)) multiplexer_1 (.sel(reset), .in_0(newNum3), .in_1({8{1'b0}}), .out(multiplexer_1_out));
  Multiplexer multiplexer_2 (.sel(reset), .in_0(loadNum3), .in_1(1'b1), .out(multiplexer_2_out));
  Multiplexer #(.Bits(8)) multiplexer_3 (.sel(reset), .in_0(newNum5), .in_1({8{1'b0}}), .out(multiplexer_3_out));
  Multiplexer multiplexer_4 (.sel(reset), .in_0(loadNum3), .in_1(1'b1), .out(multiplexer_4_out));
  Register #(.Bits(8)) u_num3 (.D(multiplexer_1_out), .C(clock), .en(multiplexer_2_out), .Q(num3));
  Register #(.Bits(4)) u_N (.D(N), .C(clock), .en(\new ), .Q(N_t));
  Register #(.Bits(8)) u_num5 (.D(multiplexer_3_out), .C(clock), .en(multiplexer_4_out), .Q(num5));
  // Probe on num3
  // Probe on N_t
  // Probe on num5
  Div #(.Bits(4)) div_1 (.a(N_t), .b(4'b0011), .r(div_1_r));  // open: q
  Div #(.Bits(4)) div_2 (.a(N_t), .b(4'b0101), .r(div_2_r));  // open: q
  Add #(.Bits(8)) add_1 (.a(num5), .b(8'h1), .c_i(1'b0), .s(add_1_s));  // open: c_o
  Add #(.Bits(8)) add_2 (.a(num3), .b(8'h1), .c_i(1'b0), .s(add_2_s));  // open: c_o
  Comparator #(.Bits(4)) comparator_1 (.a(div_1_r), .b(4'b0000), .gt(comparator_1_gt));  // open: eq, lt
  Comparator #(.Bits(4)) comparator_2 (.a(div_2_r), .b(4'b0000), .gt(comparator_2_gt));  // open: eq, lt
  Multiplexer #(.Bits(8)) multiplexer_5 (.sel(comparator_1_gt), .in_0(add_2_s), .in_1(num3), .out(newNum3));
  Multiplexer #(.Bits(8)) multiplexer_6 (.sel(comparator_2_gt), .in_0(add_1_s), .in_1(num5), .out(newNum5));
  Multiplexer #(.Selector_Bits(2)) multiplexer_7 (
    .sel({S1, S0}), .in_0(1'b0), .in_1(1'b0), .in_2(1'b0), .in_3(1'b0), .out(multiplexer_7_out));
  Multiplexer #(.Selector_Bits(2)) multiplexer_8 (
    .sel({S1, S0}), .in_0(\new ), .in_1(1'b0), .in_2(1'b0), .in_3(1'b0), .out(multiplexer_8_out));
  Decoder #(.Selector_Bits(2)) decoder_1 (
    .sel({S1, S0}), .out_0(decoder_1_out_0), .out_1(loadNum3), .out_2(decoder_1_out_2),
    .out_3(decoder_1_out_3));
  not not_1 (busy, decoder_1_out_0);
  and and_1 (and_1_out, multiplexer_7_out, not_2_out);
  not not_2 (not_2_out, reset);
  and and_2 (and_2_out, multiplexer_8_out, not_3_out);
  not not_3 (not_3_out, reset);
  D_FF u_S1 (.D(and_1_out), .C(clock), .Q(S1));  // open: nQ
  D_FF u_S0 (.D(and_2_out), .C(clock), .Q(S0));  // open: nQ

  // Other names for the same wires on the sheet: clk = clock; inN[3:0] = N; loadNum5 = loadNum3;
  //   state[1:0] = {S1, S0}
endmodule

/* Test case T01:
 N new reset clock num3 num5 busy
 0 0   1     0     x    x    x
 0 0   1     1     x    x    x
14 1   0     0     0    0    x
14 1   0     1     0    0    1
 0 0   0     0     x    x    1
 0 0   0     1     x    x    x
 0 0   0     0     x    x    x
 0 0   0     1     x    x    x
 0 0   0     0     x    x    x
 0 0   0     1     x    x    x
 0 0   0     0     x    x    x
 0 0   0     1     x    x    x
 0 0   0     0     x    x    x
 0 0   0     1     x    x    x
 0 0   0     0     x    x    x
 0 0   0     1     x    x    x
 0 0   0     0     x    x    x
 0 0   0     1     x    x    x
 0 0   0     0     x    x    x
 0 0   0     1     x    x    x
 0 0   0     0     x    x    x
 0 0   0     1     x    x    x
 0 0   0     0     x    x    x
 0 0   0     1     x    x    x
 0 0   0     0     0    0    0
 0 0   0     1     0    0    0
15 1   0     0     0    0    x
15 1   0     1     0    0    1
 0 0   0     0     x    x    1
 0 0   0     1     x    x    x
 0 0   0     0     x    x    x
 0 0   0     1     x    x    x
 0 0   0     0     x    x    x
 0 0   0     1     x    x    x
 0 0   0     0     x    x    x
 0 0   0     1     x    x    x
 0 0   0     0     x    x    x
 0 0   0     1     x    x    x
 0 0   0     0     x    x    x
 0 0   0     1     x    x    x
 0 0   0     0     x    x    x
 0 0   0     1     x    x    x
 0 0   0     0     x    x    x
 0 0   0     1     x    x    x
 0 0   0     0     x    x    x
 0 0   0     1     x    x    x
 0 0   0     0     x    x    x
 0 0   0     1     x    x    x
 0 0   0     0     1    1    0
 0 0   0     1     1    1    0
*/
