// Digital circuit Quiz1_Ex1_01.dig as structural Verilog
module Quiz1_Ex1_01 (
  input  I0,
  input  I1,
  input  I2,
  output O0,
  output O1,
  output O2
);

  Multiplexer #(.Bits(3), .Selector_Bits(3)) multiplexer_1 (
    .sel({I0, I1, I2}), .in_0(3'b000), .in_1(3'b001), .in_2(3'b011), .in_3(3'b010), .in_4(3'b110),
    .in_5(3'b111), .in_6(3'b101), .in_7(3'b100), .out({O2, O1, O0}));
endmodule
