// Digital circuit Quiz1_Ex1_02.dig as structural Verilog
module Quiz1_Ex1_02 (
  input  in_1,
  input  in_2,
  input  in_3,
  input  in_4,
  input  in_5,
  input  in_6,
  input  in_7,
  input  in_8,
  output out_9,
  output [2:0] out_10,
  output [2:0] out_11
);

  BitCount #(.Bits(5)) bitcount_1 (.in({in_5, in_4, in_3, in_2, in_1}), .out(out_10));
  BitCount #(.Bits(5)) bitcount_2 (.in({2'b00, in_8, in_7, in_6}), .out(out_11));
  Comparator #(.Bits(3)) comparator_1 (.a(out_10), .b(out_11), .eq(out_9));  // open: gt, lt
endmodule
