// Digital circuit Quiz1_Ex2_01.dig as structural Verilog
module Quiz1_Ex2_01 (
  input  A,
  input  A_2,
  input  A_3,
  input  B,
  input  B_2,
  input  B_3
);

  wire [0:0] comparator_1_eq;

  Comparator #(.Bits(4)) comparator_1 (
    .a({1'b0, A_3, A_2, A}), .b({1'b0, B_3, B_2, B}), .eq(comparator_1_eq[0]));  // open: gt, lt
  Seven_Seg_Hex seven_seg_hex_1 (.d({3'b000, comparator_1_eq[0]}), .dp(1'b0));
endmodule
