// Digital circuit Quiz1_Ex2_02.dig as structural Verilog
module Quiz1_Ex2_02 (
  input  S1,
  input  S2,
  input  S0,
  output out_2
);

  wire decoder_1_out_1, decoder_1_out_2, decoder_1_out_5, decoder_1_out_6;

  Decoder #(.Selector_Bits(3)) decoder_1 (
    .sel({S0, S1, S2}), .out_1(decoder_1_out_1), .out_2(decoder_1_out_2), .out_5(decoder_1_out_5),
    .out_6(decoder_1_out_6));  // open: out_0, out_3, out_4, out_7
  or or_1 (out_2, decoder_1_out_1, decoder_1_out_2, decoder_1_out_5, decoder_1_out_6);
endmodule
