// Digital circuit Quiz2_Ex1_01.dig as structural Verilog
module Quiz2_Ex1_01 (
  input  [7:0] A,
  input  Add,
  input  Start,
  input  clk,
  input  reset,
  output [11:0] Now
);

  wire and_1_out, and_2_out, Busy, decoder_1_out_0, decoder_1_out_1, decoder_1_out_2, decoder_1_out_3,
       loadNow, multiplexer_2_out, multiplexer_3_out, not_2_out, reset_t, S0, S1;
  wire [11:0] multiplexer_1_out, Now_new;

  Multiplexer #(.Bits(12)) multiplexer_1 (.sel(Busy), .in_0({4'b0000, A}), .in_1(Now_new), .out(multiplexer_1_out));
  Register #(.Bits(12)) u_Now (.D(multiplexer_1_out), .C(clk), .en(loadNow), .Q(Now));
  // Probe on Now
  not not_1 (reset_t, reset);
  Add #(.Bits(12)) add_1 (.a(Now), .b(12'h1), .c_i(1'b0), .s(Now_new));  // open: c_o
  Seven_Seg_Hex seven_seg_hex_1 (.d(Now[11:8]), .dp(1'b0));
  Seven_Seg_Hex seven_seg_hex_2 (.d(Now[7:4]), .dp(1'b0));
  Seven_Seg_Hex seven_seg_hex_3 (.d(Now[3:0]), .dp(1'b0));
  not not_2 (not_2_out, Add);
  Multiplexer #(.Selector_Bits(2)) multiplexer_2 (
    .sel({S1, S0}), .in_0(1'b0), .in_1(Add), .in_2(1'b0), .in_3(1'b0), .out(multiplexer_2_out));
  Multiplexer #(.Selector_Bits(2)) multiplexer_3 (
    .sel({S1, S0}), .in_0(Start), .in_1(not_2_out), .in_2(1'b1), .in_3(1'b0), .out(multiplexer_3_out));
  Decoder #(.Selector_Bits(2)) decoder_1 (
    .sel({S1, S0}), .out_0(decoder_1_out_0), .out_1(decoder_1_out_1), .out_2(decoder_1_out_2),
    .out_3(decoder_1_out_3));
  or or_1 (loadNow, decoder_1_out_2, decoder_1_out_0);
  and and_1 (and_1_out, multiplexer_2_out, reset_t);
  and and_2 (and_2_out, multiplexer_3_out, reset_t);
  not not_3 (Busy, decoder_1_out_0);
  D_FF d_ff_1 (.D(and_1_out), .C(clk), .Q(S1));  // open: nQ
  D_FF d_ff_2 (.D(and_2_out), .C(clk), .Q(S0));  // open: nQ

  // Other names for the same wires on the sheet: A_t[7:0] = A; state[1:0] = {S1, S0}
endmodule
